# Fritzing sketch temp-sensor-nodejs (saved by Fritzing 0.9.3b)
breadboards: 1

parts:
  Part1 = Arduino Uno (Rev3)
  T1 = TMP36 Temperature Sensor [package="TO92 [THT]"]
  LED1 = RGB LED - (4 legs) [package="5 mm [THT]"]

nets:
  N1: Part1.A1, T1.Vout
  N2: Part1.D3_PWM, LED1.blue_cathode
  N3: Part1.D5_PWM, LED1.green_cathode
  N4: Part1.D6_PWM, LED1.red_cathode
  N5: Part1.5V, T1.+Vs, LED1.common_anode
  GND: Part1.GND, T1.GND
