# Fritzing sketch temp-sensor-nodejs_nano (saved by Fritzing 0.9.3b)
breadboards: 1

parts:
  Part2 = Arduino Nano (Rev3.0)
  LED2 = RGB LED - (4 legs) [package="5 mm [THT]"]
  T2 = TMP36 Temperature Sensor [package="TO92 [THT]"]

nets:
  N1: Part2.D1/TX, LED2.common_anode, T2.Vout
  N2: Part2.D0/RX, Part2.D3
  N3: Part2.D2, Part2.A3
  N4: Part2.D5, LED2.blue_cathode
  N5: Part2.D6, LED2.red_cathode
  N6: Part2.D8, Part2.A0
  N7: Part2.D10, T2.+Vs
  N8: Part2.5V, Part2.A5
